# Fritzing sketch nodeMCU_sensors (saved by Fritzing 0.9.3b)
breadboards: 1

parts:
  U1 = NodeMCU V1.0
  DHT1 = DHT22 Humidity and Temperature Sensor
  R1 = Resistor [tolerance=±5% resistance=220 package="2512 [SMD]"]
  Bauteil1 = BH1750

nets:
  N1: U1.D2, DHT1.DATA, R1.Pin_0
  3V3: U1.3V3, DHT1.VDD, R1.Pin_1, Bauteil1.VCC
  GND: U1.GND, DHT1.GND, Bauteil1.GND

custom parts:
  NodeMCU V1.0: ESP8266 based NodeMCU
  BH1750: Light Sensor
