# Fritzing sketch nodeMCU_sensors_with_LCD (saved by Fritzing 0.9.3b)
breadboards: 2

parts:
  Bauteil3 = SRF05 Ultrasonic Rangefinder
  S2 = Momentary Switch [package=ksa_sealed_tac_switch]
  U2 = NodeMCU V1.0  # not connected
  DHT2 = DHT22 Humidity and Temperature Sensor
  R3 = Resistor [tolerance=±5% resistance=10k package="2512 [SMD]"]
  U5 = NodeMCU V1.0
  U6 = 74HC595 [package="DIP16 [THT]"]
  U7 = LCD-16X2 [package=lcd-16x2_noholes]
  R5 = Rotary Potentiometer (Small) [maximum_resistance=100kΩ package=THT]
  U8 = 74HC595 [package="DIP16 [THT]"]
  U9 = LCD-16X2 [package=lcd-16x2_noholes]
  R6 = Rotary Potentiometer (Small) [maximum_resistance=100kΩ package=THT]
  Bauteil5 = BH1750
  J1 = female pin header, 4 pins [form="♀ (female)"]
  J2 = female pin header, 4 pins [form="♀ (female)"]

nets:
  N1: Bauteil3.VCC, J2.pin4
  N2: Bauteil3.Trig, J2.pin3
  N3: Bauteil3.Echo, J2.pin2
  N4: Bauteil3.GND, J2.pin1
  N5: S2.2, R3.Pin_1
  VDD: S2.4, DHT2.VDD, U8.MR, U8.VCC, U9.VDD, Bauteil5.VCC, J1.pin4
  GND: DHT2.GND, R3.Pin_0, U8.GND, U8.OE, U9.VSS, U9.R_W, U9.K, Bauteil5.GND, Bauteil5.ADDR, J1.pin1
  N6: U5.D2, U6.ST_CP
  N7: U5.3V3, U7.A
  N8: U5.GND, U6.OE
  N9: U5.D5, U6.SH_CP
  N10: U5.D7, U6.DS
  N11: U6.Q1, U7.RS
  N12: U6.Q3, U7.E
  N13: U6.Q4, U7.DB4
  N14: U6.Q5, U7.DB5
  N15: U6.Q6, U7.DB6
  N16: U6.Q7, U7.DB7
  GND_2: U6.GND, U7.VSS, U7.R_W, U7.K, R5.leg2
  N17: U6.MR, U6.VCC
  N18: U7.VDD, R5.leg1
  N19: U7.VO, R5.wiper
  N20: U8.Q1, U9.RS
  N21: U8.Q3, U9.E
  N22: U8.Q4, U9.DB4
  N23: U8.Q5, U9.DB5
  N24: U8.Q6, U9.DB6
  N25: U8.Q7, U9.DB7
  N26: U9.VO, R6.wiper

custom parts:
  NodeMCU V1.0: ESP8266 based NodeMCU
  BH1750: Light Sensor
